# Fritzing sketch Self-Watering Plant Sensor (saved by Fritzing 0.9.3b)
breadboards: 1

parts:
  Part2 = songle relay
  Parts1 = SparkFun RedBoard [part_number=DEV-12757]
  Part3 = Soil Moisture Sensor
  J1 = Power Jack [package=power_jack_pth]
  M1 = DC Motor
  Water_Level_Sensor1 = Water Level Sensor

nets:
  VCC: Part2.VCC, Parts1.5V, Water_Level_Sensor1.VCC
  N1: Part2.NO, M1.pin_1
  N2: Part2.NC, J1.GND
  N3: Part2.COMMON, Parts1.D8
  GND: Part2.GND, Parts1.GND, Part3.GND, Water_Level_Sensor1.GND
  N4: Parts1.A0, Part3.SIG
  N5: Parts1.A1, Water_Level_Sensor1.SIG
  N6: Parts1.D7, Part3.VCC
  N7: J1.PWR, M1.pin_2

notes:
  Water Sensor for detecting how much water is left in the parent container.
  Submersible water pump used to transport the water from the parent container to the plant container
  9v DC power coming from an outlet to the breadboard directly.
  Power Relay used to complete the circuit for the submersible water pump if it is turned on by the Sparkfun Board
  Moisture Sensor to detect how dry the plant is. The logic to determine how dry is too dry is currently set as a variable on runtime and it can not be changed.
  IF the Mositure Sensor detects that the plant is too dry AND the Water Sensor detects water, THEN activate the pump via the relay.

custom parts:
  SparkFun RedBoard: At SparkFun we use many Arduinos and we’re always looking for the simplest, most stable one. Each board is a bit different and no one board has everything we want, so we decided to make our own version that combines all our favorite features. The RedBoard combines the simplicity of the UNO’s Optiboot bootloader (which is used in the Pro series), the stability of the FTDI (which we all missed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
  Water Level Sensor: A water level sensor. This sensor operates at 3V to 5V. The Sig (signal) pin outputs an analogue signal that is in proportion to the amount of water in contact with the sensor.
